// Logisim project AMFB-16.circ as structural Verilog: 29 circuits, main circuit testing
module testing (
  input  in_1,
  input  in_2,
  input  in_3,
  input  in_4,
  input  in_5,
  input  in_6,
  input  in_7,
  input  in_8,
  input  in_9,
  input  in_10,
  input  in_11,
  input  in_12,
  input  in_13,
  input  in_14,
  input  in_15,
  input  in_16,
  input  in_17,
  input  in_18,
  input  in_19,
  input  in_20,
  input  in_21,
  input  in_22,
  input  in_23,
  input  in_24,
  input  in_25,
  input  in_26,
  input  in_27,
  input  in_28,
  input  in_29,
  input  in_30,
  input  in_31,
  input  in_32,
  input  in_33,
  input  in_34,
  input  in_35,
  input  in_36,
  input  in_37
);

  wire [5:0] alu_1_flagsbus;
  wire [15:0] alu_1_highoutput, alu_1_lowoutput;

  LED led_1 (.in(alu_1_highoutput[0]));
  LED led_2 (.in(alu_1_highoutput[1]));
  LED led_3 (.in(alu_1_highoutput[2]));
  LED led_4 (.in(alu_1_highoutput[3]));
  LED led_5 (.in(alu_1_highoutput[4]));
  LED led_6 (.in(alu_1_highoutput[5]));
  LED led_7 (.in(alu_1_highoutput[6]));
  LED led_8 (.in(alu_1_highoutput[7]));
  LED led_9 (.in(alu_1_highoutput[8]));
  LED led_10 (.in(alu_1_highoutput[9]));
  LED led_11 (.in(alu_1_highoutput[10]));
  LED led_12 (.in(alu_1_highoutput[11]));
  LED led_13 (.in(alu_1_highoutput[12]));
  LED led_14 (.in(alu_1_highoutput[13]));
  LED led_15 (.in(alu_1_highoutput[14]));
  LED led_16 (.in(alu_1_highoutput[15]));
  ALU alu_1 (
    .AInput({in_31, in_29, in_27, in_25, in_23, in_21, in_19, in_17, in_15, in_13, in_11, in_9, in_7, in_5, in_3, in_1}),
    .BInput({in_32, in_30, in_28, in_26, in_24, in_22, in_20, in_18, in_16, in_14, in_12, in_10, in_8, in_6, in_4, in_2}),
    .Cin(in_36), .ControlInput({in_37, in_35, in_34, in_33}), .HighOutput(alu_1_highoutput),
    .LowOutput(alu_1_lowoutput), .FlagsBus(alu_1_flagsbus));
  LED led_17 (.in(alu_1_lowoutput[0]));
  LED led_18 (.in(alu_1_lowoutput[1]));
  LED led_19 (.in(alu_1_lowoutput[2]));
  LED led_20 (.in(alu_1_lowoutput[3]));
  LED led_21 (.in(alu_1_lowoutput[4]));
  LED led_22 (.in(alu_1_lowoutput[5]));
  LED led_23 (.in(alu_1_lowoutput[6]));
  LED led_24 (.in(alu_1_lowoutput[7]));
  LED led_25 (.in(alu_1_lowoutput[8]));
  LED led_26 (.in(alu_1_lowoutput[9]));
  LED led_27 (.in(alu_1_lowoutput[10]));
  LED led_28 (.in(alu_1_lowoutput[11]));
  LED led_29 (.in(alu_1_lowoutput[12]));
  LED led_30 (.in(alu_1_flagsbus[0]));
  LED led_31 (.in(alu_1_lowoutput[13]));
  LED led_32 (.in(alu_1_flagsbus[1]));
  LED led_33 (.in(alu_1_lowoutput[14]));
  LED led_34 (.in(alu_1_flagsbus[2]));
  LED led_35 (.in(alu_1_lowoutput[15]));
  LED led_36 (.in(alu_1_flagsbus[3]));
  LED led_37 (.in(alu_1_flagsbus[4]));
  LED led_38 (.in(alu_1_flagsbus[5]));

  // Other names for the same wires on the sheet: AInput[15:0] = {in_31, in_29, in_27, in_25, in_23, in_21, in_19, in_17, in_15, in_13, in_11, in_9, in_7, in_5, in_3, in_1};
  //   BInput[15:0] = {in_32, in_30, in_28, in_26, in_24, in_22, in_20, in_18, in_16, in_14, in_12, in_10, in_8, in_6, in_4, in_2}
endmodule

module ALU (
  input  [15:0] AInput,
  input  [15:0] BInput,
  input  Cin,
  input  [3:0] ControlInput,
  output [15:0] HighOutput,
  output [15:0] LowOutput,
  output [5:0] FlagsBus
);

  wire addsub_1_cout, and_1_out, and_2_out, and_3_out, and_4_out, and_5_out, and_6_out, and_7_out,
       multiply_1_overflowbus, not_1_out, not_2_out, not_3_out, not_4_out, not_5_out, not_6_out, not_7_out,
       not_8_out, or_3_out;
  wire [15:0] addsub_1_numberoutput, and_8_out, and_9_out, and_10_out, and_11_out, and_13_out, and_14_out,
       bit_extender_1_out, bit_extender_2_out, bit_extender_3_out, bit_extender_4_out, bit_extender_5_out,
       bit_extender_6_out, logicgates_1_dataoutput, multiply_1_highoutput, multiply_1_lowoutput, or_1_out,
       popcount_1_dataoutput, rotshift_1_numberoutput;

  not not_1 (not_1_out, ControlInput[0]);
  not not_2 (not_2_out, ControlInput[1]);
  not not_3 (not_3_out, ControlInput[2]);
  not not_4 (not_4_out, ControlInput[1]);
  not not_5 (not_5_out, ControlInput[3]);
  not not_6 (not_6_out, ControlInput[1]);
  assign bit_extender_1_out = {{15{and_1_out}}, and_1_out};  // Bit_Extender bit_extender_1
  and and_1 (and_1_out, ControlInput[3], ControlInput[2], ControlInput[1], ControlInput[0]);
  not not_7 (not_7_out, ControlInput[0]);
  and and_2 (and_2_out, not_7_out, not_8_out);
  not not_8 (not_8_out, ControlInput[1]);
  assign bit_extender_2_out = {{15{and_3_out}}, and_3_out};  // Bit_Extender bit_extender_2
  and and_3 (and_3_out, not_1_out, ControlInput[1]);
  assign bit_extender_3_out = {{15{and_4_out}}, and_4_out};  // Bit_Extender bit_extender_3
  and and_4 (and_4_out, ControlInput[0], not_2_out, not_3_out);
  assign bit_extender_4_out = {{15{and_5_out}}, and_5_out};  // Bit_Extender bit_extender_4
  and and_5 (and_5_out, ControlInput[0], not_4_out, ControlInput[2], not_5_out);
  assign bit_extender_5_out = {{15{and_6_out}}, and_6_out};  // Bit_Extender bit_extender_5
  and and_6 (and_6_out, ControlInput[0], not_6_out, ControlInput[2], ControlInput[3]);
  assign bit_extender_6_out = {{15{and_2_out}}, and_2_out};  // Bit_Extender bit_extender_6
  and and_7 (and_7_out, Cin, ControlInput[3]);
  assign and_8_out = AInput & bit_extender_1_out;  // AND_Gate and_8, 16 bits wide
  logicgates logicgates_1 (
    .AInput(AInput), .BInput(BInput), .Operation(ControlInput[3:2]), .DataOutput(logicgates_1_dataoutput));
  rotshift rotshift_1 (
    .ShiftCount(BInput), .RolInput(Cin), .Number(AInput), .SideShift(ControlInput[3]),
    .NumberOutput(rotshift_1_numberoutput));
  multiply multiply_1 (
    .AInput(AInput), .BInput(BInput), .OverflowBus(multiply_1_overflowbus),
    .HighOutput(multiply_1_highoutput), .LowOutput(multiply_1_lowoutput));
  popcount popcount_1 (.DataInput(AInput), .DataOutput(popcount_1_dataoutput));
  assign and_9_out = popcount_1_dataoutput & bit_extender_5_out;  // AND_Gate and_9, 16 bits wide
  addsub addsub_1 (
    .AInput(AInput), .BInput(BInput), .Operation(ControlInput[2]), .Cin(and_7_out), .Cout(addsub_1_cout),
    .Vout(FlagsBus[2]), .NumberOutput(addsub_1_numberoutput));
  assign and_10_out = rotshift_1_numberoutput & bit_extender_3_out;  // AND_Gate and_10, 16 bits wide
  assign and_11_out = multiply_1_lowoutput & bit_extender_4_out;  // AND_Gate and_11, 16 bits wide
  assign HighOutput = multiply_1_highoutput & bit_extender_4_out;  // AND_Gate and_12, 16 bits wide
  assign or_1_out = {LowOutput[15:1], FlagsBus[3]} | HighOutput;  // OR_Gate or_1, 16 bits wide
  assign {LowOutput[15:1], FlagsBus[3]} = and_8_out | and_11_out | and_10_out | and_9_out | and_14_out | and_13_out;  // OR_Gate or_2, 16 bits wide
  assign and_13_out = bit_extender_6_out & addsub_1_numberoutput;  // AND_Gate and_13, 16 bits wide
  assign and_14_out = bit_extender_2_out & logicgates_1_dataoutput;  // AND_Gate and_14, 16 bits wide
  and and_15 (FlagsBus[4], multiply_1_overflowbus, and_5_out);
  and and_16 (FlagsBus[1], and_2_out, addsub_1_cout);
  and and_17 (FlagsBus[0], or_3_out, FlagsBus[1]);
  not not_9 (FlagsBus[5], or_3_out);
  or or_3 (or_3_out, or_1_out[0], or_1_out[1], or_1_out[2], or_1_out[3], or_1_out[4], or_1_out[5], or_1_out[6], or_1_out[7], or_1_out[8], or_1_out[9], or_1_out[10], or_1_out[11], or_1_out[12], or_1_out[13], or_1_out[14], or_1_out[15]);

  assign LowOutput[0] = FlagsBus[3];
endmodule

module popcount (
  input  [15:0] DataInput,
  output [15:0] DataOutput
);

  wire [1:0] minihalfadder_1_dataoutput, minihalfadder_2_dataoutput, minihalfadder_3_dataoutput,
       minihalfadder_4_dataoutput, minihalfadder_5_dataoutput, minihalfadder_6_dataoutput,
       minihalfadder_7_dataoutput, minihalfadder_8_dataoutput;
  wire [2:0] popcountadder0_1_out_3, popcountadder0_2_out_3, popcountadder0_3_out_3, popcountadder0_4_out_3;
  wire [3:0] popcountadder1_1_dataoutput, popcountadder1_2_dataoutput;

  minihalfadder minihalfadder_1 (.AInput(DataInput[0]), .BInput(DataInput[1]), .DataOutput(minihalfadder_1_dataoutput));
  minihalfadder minihalfadder_2 (.AInput(DataInput[2]), .BInput(DataInput[3]), .DataOutput(minihalfadder_2_dataoutput));
  minihalfadder minihalfadder_3 (.AInput(DataInput[4]), .BInput(DataInput[5]), .DataOutput(minihalfadder_3_dataoutput));
  minihalfadder minihalfadder_4 (.AInput(DataInput[6]), .BInput(DataInput[7]), .DataOutput(minihalfadder_4_dataoutput));
  minihalfadder minihalfadder_5 (.AInput(DataInput[8]), .BInput(DataInput[9]), .DataOutput(minihalfadder_5_dataoutput));
  minihalfadder minihalfadder_6 (
    .AInput(DataInput[10]), .BInput(DataInput[11]), .DataOutput(minihalfadder_6_dataoutput));
  minihalfadder minihalfadder_7 (
    .AInput(DataInput[12]), .BInput(DataInput[13]), .DataOutput(minihalfadder_7_dataoutput));
  minihalfadder minihalfadder_8 (
    .AInput(DataInput[14]), .BInput(DataInput[15]), .DataOutput(minihalfadder_8_dataoutput));
  popcountadder0 popcountadder0_1 (
    .AInput(minihalfadder_1_dataoutput), .BInput(minihalfadder_2_dataoutput), .out_3(popcountadder0_1_out_3));
  popcountadder0 popcountadder0_2 (
    .AInput(minihalfadder_3_dataoutput), .BInput(minihalfadder_4_dataoutput), .out_3(popcountadder0_2_out_3));
  popcountadder0 popcountadder0_3 (
    .AInput(minihalfadder_5_dataoutput), .BInput(minihalfadder_6_dataoutput), .out_3(popcountadder0_3_out_3));
  popcountadder0 popcountadder0_4 (
    .AInput(minihalfadder_7_dataoutput), .BInput(minihalfadder_8_dataoutput), .out_3(popcountadder0_4_out_3));
  popcountadder1 popcountadder1_1 (
    .AInput(popcountadder0_1_out_3), .BInput(popcountadder0_2_out_3), .DataOutput(popcountadder1_1_dataoutput));
  popcountadder1 popcountadder1_2 (
    .AInput(popcountadder0_3_out_3), .BInput(popcountadder0_4_out_3), .DataOutput(popcountadder1_2_dataoutput));
  halfbyteadder halfbyteadder_1 (
    .AInput(popcountadder1_1_dataoutput), .BInput(popcountadder1_2_dataoutput), .DataOutput(DataOutput[15:11]));

  assign DataOutput[10:0] = {11{1'b0}};
endmodule

module rotshift (
  input  [15:0] ShiftCount,
  input  RolInput,
  input  [15:0] Number,
  input  SideShift,
  output [15:0] NumberOutput
);

  wire rolshift1_1_roloutput, rolshift2_1_roloutput, rolshift4_1_roloutput;
  wire [15:0] and_1_out, and_2_out, and_3_out, and_4_out, and_5_out, and_6_out, and_7_out, and_8_out,
       and_9_out, and_10_out, and_11_out, and_12_out, bit_extender_1_out, bit_extender_2_out,
       bit_extender_3_out, bit_extender_4_out, bit_extender_5_out, bit_extender_6_out, not_1_out, not_2_out,
       not_3_out, not_4_out, not_5_out, not_6_out, or_1_out, or_2_out, or_3_out, or_4_out, or_5_out,
       reverse_1_dataoutput, reverse_2_dataoutput, rolshift1_1_dataoutput, rolshift2_1_dataoutput,
       rolshift4_1_dataoutput, rolshift8_1_dataoutput;

  assign bit_extender_1_out = {{15{SideShift}}, SideShift};  // Bit_Extender bit_extender_1
  assign not_1_out = ~bit_extender_1_out;  // NOT_Gate not_1, 16 bits wide
  reverse reverse_1 (.DataInput(Number), .DataOutput(reverse_1_dataoutput));
  assign and_1_out = Number & not_1_out;  // AND_Gate and_1, 16 bits wide
  assign and_2_out = reverse_1_dataoutput & bit_extender_1_out;  // AND_Gate and_2, 16 bits wide
  assign or_1_out = and_2_out | and_1_out;  // OR_Gate or_1, 16 bits wide
  assign bit_extender_2_out = {{15{ShiftCount[15]}}, ShiftCount[15]};  // Bit_Extender bit_extender_2
  assign not_2_out = ~bit_extender_2_out;  // NOT_Gate not_2, 16 bits wide
  assign and_3_out = bit_extender_2_out & or_1_out;  // AND_Gate and_3, 16 bits wide
  assign and_4_out = or_1_out & not_2_out;  // AND_Gate and_4, 16 bits wide
  rolshift1 rolshift1_1 (
    .RolInput(RolInput), .DataInput(and_3_out), .RolOutput(rolshift1_1_roloutput),
    .DataOutput(rolshift1_1_dataoutput));
  assign or_2_out = rolshift1_1_dataoutput | and_4_out;  // OR_Gate or_2, 16 bits wide
  assign bit_extender_3_out = {{15{ShiftCount[14]}}, ShiftCount[14]};  // Bit_Extender bit_extender_3
  assign not_3_out = ~bit_extender_3_out;  // NOT_Gate not_3, 16 bits wide
  assign and_5_out = bit_extender_3_out & or_2_out;  // AND_Gate and_5, 16 bits wide
  assign and_6_out = or_2_out & not_3_out;  // AND_Gate and_6, 16 bits wide
  rolshift2 rolshift2_1 (
    .RolInput(rolshift1_1_roloutput), .DataInput(and_5_out), .RolOutput(rolshift2_1_roloutput),
    .DataOutput(rolshift2_1_dataoutput));
  assign or_3_out = rolshift2_1_dataoutput | and_6_out;  // OR_Gate or_3, 16 bits wide
  assign bit_extender_4_out = {{15{ShiftCount[13]}}, ShiftCount[13]};  // Bit_Extender bit_extender_4
  assign not_4_out = ~bit_extender_4_out;  // NOT_Gate not_4, 16 bits wide
  assign and_7_out = bit_extender_4_out & or_3_out;  // AND_Gate and_7, 16 bits wide
  assign and_8_out = or_3_out & not_4_out;  // AND_Gate and_8, 16 bits wide
  rolshift4 rolshift4_1 (
    .RolInput(rolshift2_1_roloutput), .DataInput(and_7_out), .RolOutput(rolshift4_1_roloutput),
    .DataOutput(rolshift4_1_dataoutput));
  assign or_4_out = rolshift4_1_dataoutput | and_8_out;  // OR_Gate or_4, 16 bits wide
  assign bit_extender_5_out = {{15{ShiftCount[12]}}, ShiftCount[12]};  // Bit_Extender bit_extender_5
  assign not_5_out = ~bit_extender_5_out;  // NOT_Gate not_5, 16 bits wide
  assign and_9_out = bit_extender_5_out & or_4_out;  // AND_Gate and_9, 16 bits wide
  assign and_10_out = or_4_out & not_5_out;  // AND_Gate and_10, 16 bits wide
  rolshift8 rolshift8_1 (
    .RolInput(rolshift4_1_roloutput), .DataInput(and_9_out), .DataOutput(rolshift8_1_dataoutput));  // open: RolOutput
  assign or_5_out = rolshift8_1_dataoutput | and_10_out;  // OR_Gate or_5, 16 bits wide
  assign bit_extender_6_out = {{15{SideShift}}, SideShift};  // Bit_Extender bit_extender_6
  assign not_6_out = ~bit_extender_6_out;  // NOT_Gate not_6, 16 bits wide
  reverse reverse_2 (.DataInput(or_5_out), .DataOutput(reverse_2_dataoutput));
  assign and_11_out = or_5_out & not_6_out;  // AND_Gate and_11, 16 bits wide
  assign and_12_out = reverse_2_dataoutput & bit_extender_6_out;  // AND_Gate and_12, 16 bits wide
  assign NumberOutput = and_12_out | and_11_out;  // OR_Gate or_6, 16 bits wide
endmodule

module reverse (
  input  [15:0] DataInput,
  output [15:0] DataOutput
);


  assign DataOutput = {DataInput[0], DataInput[1], DataInput[2], DataInput[3], DataInput[4], DataInput[5], DataInput[6], DataInput[7], DataInput[8], DataInput[9], DataInput[10], DataInput[11], DataInput[12], DataInput[13], DataInput[14], DataInput[15]};
endmodule

module shift1 (
  input  [31:0] DataInput,
  output [31:0] DataOutput
);


  assign DataOutput = {1'b0, DataInput[31:1]};
endmodule

module multiply (
  input  [15:0] AInput,
  input  [15:0] BInput,
  output OverflowBus,
  output [15:0] HighOutput,
  output [15:0] LowOutput
);

  wire [15:0] and_1_out, and_2_out, and_3_out, and_4_out, and_5_out, and_6_out, and_7_out, and_8_out,
       and_9_out, and_10_out, and_11_out, and_12_out, and_13_out, and_14_out, and_15_out, and_16_out,
       bit_extender_1_out, bit_extender_2_out, bit_extender_3_out, bit_extender_4_out, bit_extender_5_out,
       bit_extender_6_out, bit_extender_7_out, bit_extender_8_out, bit_extender_9_out, bit_extender_10_out,
       bit_extender_11_out, bit_extender_12_out, bit_extender_13_out, bit_extender_14_out,
       bit_extender_15_out, bit_extender_16_out;
  wire [31:0] megaadder_1_dataoutput, megaadder_2_dataoutput, megaadder_3_dataoutput, megaadder_4_dataoutput,
       megaadder_5_dataoutput, megaadder_6_dataoutput, megaadder_7_dataoutput, megaadder_8_dataoutput,
       megaadder_9_dataoutput, megaadder_10_dataoutput, megaadder_11_dataoutput, megaadder_12_dataoutput,
       megaadder_13_dataoutput, megaadder_14_dataoutput, shift1_1_dataoutput, shift1_2_dataoutput,
       shift1_3_dataoutput, shift1_4_dataoutput, shift1_5_dataoutput, shift1_6_dataoutput,
       shift1_7_dataoutput, shift1_8_dataoutput, shift2_1_dataoutput, shift2_2_dataoutput,
       shift2_3_dataoutput, shift2_4_dataoutput, shift2_5_dataoutput, shift2_6_dataoutput,
       shift2_7_dataoutput, shift2_8_dataoutput, shift4_1_dataoutput, shift4_2_dataoutput,
       shift4_3_dataoutput, shift4_4_dataoutput, shift4_5_dataoutput, shift4_6_dataoutput,
       shift4_7_dataoutput, shift4_8_dataoutput, shift8_1_dataoutput, shift8_2_dataoutput,
       shift8_3_dataoutput, shift8_4_dataoutput, shift8_5_dataoutput, shift8_6_dataoutput,
       shift8_7_dataoutput, shift8_8_dataoutput, shorttoint_1_dataoutput, shorttoint_2_dataoutput,
       shorttoint_3_dataoutput, shorttoint_4_dataoutput, shorttoint_5_dataoutput, shorttoint_6_dataoutput,
       shorttoint_7_dataoutput, shorttoint_8_dataoutput, shorttoint_9_dataoutput, shorttoint_10_dataoutput,
       shorttoint_11_dataoutput, shorttoint_12_dataoutput, shorttoint_13_dataoutput,
       shorttoint_14_dataoutput, shorttoint_15_dataoutput, shorttoint_16_dataoutput;

  assign bit_extender_1_out = {{15{BInput[0]}}, BInput[0]};  // Bit_Extender bit_extender_1
  assign bit_extender_2_out = {{15{BInput[1]}}, BInput[1]};  // Bit_Extender bit_extender_2
  assign bit_extender_3_out = {{15{BInput[2]}}, BInput[2]};  // Bit_Extender bit_extender_3
  assign bit_extender_4_out = {{15{BInput[3]}}, BInput[3]};  // Bit_Extender bit_extender_4
  assign bit_extender_5_out = {{15{BInput[4]}}, BInput[4]};  // Bit_Extender bit_extender_5
  assign bit_extender_6_out = {{15{BInput[5]}}, BInput[5]};  // Bit_Extender bit_extender_6
  assign bit_extender_7_out = {{15{BInput[6]}}, BInput[6]};  // Bit_Extender bit_extender_7
  assign bit_extender_8_out = {{15{BInput[7]}}, BInput[7]};  // Bit_Extender bit_extender_8
  assign bit_extender_9_out = {{15{BInput[8]}}, BInput[8]};  // Bit_Extender bit_extender_9
  assign bit_extender_10_out = {{15{BInput[9]}}, BInput[9]};  // Bit_Extender bit_extender_10
  assign bit_extender_11_out = {{15{BInput[10]}}, BInput[10]};  // Bit_Extender bit_extender_11
  assign bit_extender_12_out = {{15{BInput[11]}}, BInput[11]};  // Bit_Extender bit_extender_12
  assign bit_extender_13_out = {{15{BInput[12]}}, BInput[12]};  // Bit_Extender bit_extender_13
  assign bit_extender_14_out = {{15{BInput[13]}}, BInput[13]};  // Bit_Extender bit_extender_14
  assign bit_extender_15_out = {{15{BInput[14]}}, BInput[14]};  // Bit_Extender bit_extender_15
  assign bit_extender_16_out = {{15{BInput[15]}}, BInput[15]};  // Bit_Extender bit_extender_16
  assign and_1_out = AInput & bit_extender_1_out;  // AND_Gate and_1, 16 bits wide
  assign and_2_out = AInput & bit_extender_2_out;  // AND_Gate and_2, 16 bits wide
  assign and_3_out = AInput & bit_extender_3_out;  // AND_Gate and_3, 16 bits wide
  assign and_4_out = AInput & bit_extender_4_out;  // AND_Gate and_4, 16 bits wide
  assign and_5_out = AInput & bit_extender_5_out;  // AND_Gate and_5, 16 bits wide
  assign and_6_out = AInput & bit_extender_6_out;  // AND_Gate and_6, 16 bits wide
  assign and_7_out = AInput & bit_extender_7_out;  // AND_Gate and_7, 16 bits wide
  assign and_8_out = AInput & bit_extender_8_out;  // AND_Gate and_8, 16 bits wide
  assign and_9_out = AInput & bit_extender_9_out;  // AND_Gate and_9, 16 bits wide
  assign and_10_out = AInput & bit_extender_10_out;  // AND_Gate and_10, 16 bits wide
  assign and_11_out = AInput & bit_extender_11_out;  // AND_Gate and_11, 16 bits wide
  assign and_12_out = AInput & bit_extender_12_out;  // AND_Gate and_12, 16 bits wide
  assign and_13_out = AInput & bit_extender_13_out;  // AND_Gate and_13, 16 bits wide
  assign and_14_out = AInput & bit_extender_14_out;  // AND_Gate and_14, 16 bits wide
  assign and_15_out = AInput & bit_extender_15_out;  // AND_Gate and_15, 16 bits wide
  assign and_16_out = AInput & bit_extender_16_out;  // AND_Gate and_16, 16 bits wide
  shorttoint shorttoint_1 (.DataInput(and_1_out), .DataOutput(shorttoint_1_dataoutput));
  shorttoint shorttoint_2 (.DataInput(and_2_out), .DataOutput(shorttoint_2_dataoutput));
  shorttoint shorttoint_3 (.DataInput(and_3_out), .DataOutput(shorttoint_3_dataoutput));
  shorttoint shorttoint_4 (.DataInput(and_4_out), .DataOutput(shorttoint_4_dataoutput));
  shorttoint shorttoint_5 (.DataInput(and_5_out), .DataOutput(shorttoint_5_dataoutput));
  shorttoint shorttoint_6 (.DataInput(and_6_out), .DataOutput(shorttoint_6_dataoutput));
  shorttoint shorttoint_7 (.DataInput(and_7_out), .DataOutput(shorttoint_7_dataoutput));
  shorttoint shorttoint_8 (.DataInput(and_8_out), .DataOutput(shorttoint_8_dataoutput));
  shorttoint shorttoint_9 (.DataInput(and_9_out), .DataOutput(shorttoint_9_dataoutput));
  shorttoint shorttoint_10 (.DataInput(and_10_out), .DataOutput(shorttoint_10_dataoutput));
  shorttoint shorttoint_11 (.DataInput(and_11_out), .DataOutput(shorttoint_11_dataoutput));
  shorttoint shorttoint_12 (.DataInput(and_12_out), .DataOutput(shorttoint_12_dataoutput));
  shorttoint shorttoint_13 (.DataInput(and_13_out), .DataOutput(shorttoint_13_dataoutput));
  shorttoint shorttoint_14 (.DataInput(and_14_out), .DataOutput(shorttoint_14_dataoutput));
  shorttoint shorttoint_15 (.DataInput(and_15_out), .DataOutput(shorttoint_15_dataoutput));
  shorttoint shorttoint_16 (.DataInput(and_16_out), .DataOutput(shorttoint_16_dataoutput));
  shift8 shift8_1 (.DataInput(shorttoint_1_dataoutput), .DataOutput(shift8_1_dataoutput));
  shift8 shift8_2 (.DataInput(shorttoint_2_dataoutput), .DataOutput(shift8_2_dataoutput));
  shift8 shift8_3 (.DataInput(shorttoint_3_dataoutput), .DataOutput(shift8_3_dataoutput));
  shift8 shift8_4 (.DataInput(shorttoint_4_dataoutput), .DataOutput(shift8_4_dataoutput));
  shift8 shift8_5 (.DataInput(shorttoint_5_dataoutput), .DataOutput(shift8_5_dataoutput));
  shift8 shift8_6 (.DataInput(shorttoint_6_dataoutput), .DataOutput(shift8_6_dataoutput));
  shift8 shift8_7 (.DataInput(shorttoint_7_dataoutput), .DataOutput(shift8_7_dataoutput));
  shift8 shift8_8 (.DataInput(shorttoint_8_dataoutput), .DataOutput(shift8_8_dataoutput));
  shift4 shift4_1 (.DataInput(shorttoint_9_dataoutput), .DataOutput(shift4_1_dataoutput));
  shift4 shift4_2 (.DataInput(shorttoint_10_dataoutput), .DataOutput(shift4_2_dataoutput));
  shift4 shift4_3 (.DataInput(shorttoint_11_dataoutput), .DataOutput(shift4_3_dataoutput));
  shift4 shift4_4 (.DataInput(shorttoint_12_dataoutput), .DataOutput(shift4_4_dataoutput));
  shift2 shift2_1 (.DataInput(shorttoint_13_dataoutput), .DataOutput(shift2_1_dataoutput));
  shift2 shift2_2 (.DataInput(shorttoint_14_dataoutput), .DataOutput(shift2_2_dataoutput));
  shift1 shift1_1 (.DataInput(shorttoint_15_dataoutput), .DataOutput(shift1_1_dataoutput));
  shift4 shift4_5 (.DataInput(shift8_1_dataoutput), .DataOutput(shift4_5_dataoutput));
  shift4 shift4_6 (.DataInput(shift8_2_dataoutput), .DataOutput(shift4_6_dataoutput));
  shift4 shift4_7 (.DataInput(shift8_3_dataoutput), .DataOutput(shift4_7_dataoutput));
  shift4 shift4_8 (.DataInput(shift8_4_dataoutput), .DataOutput(shift4_8_dataoutput));
  shift2 shift2_3 (.DataInput(shift8_5_dataoutput), .DataOutput(shift2_3_dataoutput));
  shift2 shift2_4 (.DataInput(shift8_6_dataoutput), .DataOutput(shift2_4_dataoutput));
  shift1 shift1_2 (.DataInput(shift8_7_dataoutput), .DataOutput(shift1_2_dataoutput));
  shift2 shift2_5 (.DataInput(shift4_1_dataoutput), .DataOutput(shift2_5_dataoutput));
  shift2 shift2_6 (.DataInput(shift4_2_dataoutput), .DataOutput(shift2_6_dataoutput));
  shift1 shift1_3 (.DataInput(shift4_3_dataoutput), .DataOutput(shift1_3_dataoutput));
  shift1 shift1_4 (.DataInput(shift2_1_dataoutput), .DataOutput(shift1_4_dataoutput));
  shift2 shift2_7 (.DataInput(shift4_5_dataoutput), .DataOutput(shift2_7_dataoutput));
  shift2 shift2_8 (.DataInput(shift4_6_dataoutput), .DataOutput(shift2_8_dataoutput));
  shift1 shift1_5 (.DataInput(shift4_7_dataoutput), .DataOutput(shift1_5_dataoutput));
  shift1 shift1_6 (.DataInput(shift2_3_dataoutput), .DataOutput(shift1_6_dataoutput));
  shift1 shift1_7 (.DataInput(shift2_5_dataoutput), .DataOutput(shift1_7_dataoutput));
  shift1 shift1_8 (.DataInput(shift2_7_dataoutput), .DataOutput(shift1_8_dataoutput));
  megaadder megaadder_1 (
    .AInput(shift1_8_dataoutput), .BInput(shift2_8_dataoutput), .DataOutput(megaadder_1_dataoutput));
  megaadder megaadder_2 (
    .AInput(shift1_5_dataoutput), .BInput(shift4_8_dataoutput), .DataOutput(megaadder_2_dataoutput));
  megaadder megaadder_3 (
    .AInput(shift1_6_dataoutput), .BInput(shift2_4_dataoutput), .DataOutput(megaadder_3_dataoutput));
  megaadder megaadder_4 (
    .AInput(shift1_2_dataoutput), .BInput(shift8_8_dataoutput), .DataOutput(megaadder_4_dataoutput));
  megaadder megaadder_5 (
    .AInput(shift1_7_dataoutput), .BInput(shift2_6_dataoutput), .DataOutput(megaadder_5_dataoutput));
  megaadder megaadder_6 (
    .AInput(shift1_3_dataoutput), .BInput(shift4_4_dataoutput), .DataOutput(megaadder_6_dataoutput));
  megaadder megaadder_7 (
    .AInput(shift1_4_dataoutput), .BInput(shift2_2_dataoutput), .DataOutput(megaadder_7_dataoutput));
  megaadder megaadder_8 (
    .AInput(shift1_1_dataoutput), .BInput(shorttoint_16_dataoutput), .DataOutput(megaadder_8_dataoutput));
  megaadder megaadder_9 (
    .AInput(megaadder_1_dataoutput), .BInput(megaadder_2_dataoutput), .DataOutput(megaadder_9_dataoutput));
  megaadder megaadder_10 (
    .AInput(megaadder_3_dataoutput), .BInput(megaadder_4_dataoutput), .DataOutput(megaadder_10_dataoutput));
  megaadder megaadder_11 (
    .AInput(megaadder_5_dataoutput), .BInput(megaadder_6_dataoutput), .DataOutput(megaadder_11_dataoutput));
  megaadder megaadder_12 (
    .AInput(megaadder_7_dataoutput), .BInput(megaadder_8_dataoutput), .DataOutput(megaadder_12_dataoutput));
  megaadder megaadder_13 (
    .AInput(megaadder_9_dataoutput), .BInput(megaadder_10_dataoutput), .DataOutput(megaadder_13_dataoutput));
  megaadder megaadder_14 (
    .AInput(megaadder_11_dataoutput), .BInput(megaadder_12_dataoutput), .DataOutput(megaadder_14_dataoutput));
  megaadder megaadder_15 (
    .AInput(megaadder_13_dataoutput), .BInput(megaadder_14_dataoutput), .DataOutput({LowOutput, HighOutput}));
  or or_1 (OverflowBus, HighOutput[0], HighOutput[1], HighOutput[2], HighOutput[3], HighOutput[4], HighOutput[5], HighOutput[6], HighOutput[7], HighOutput[8], HighOutput[9], HighOutput[10], HighOutput[11], HighOutput[12], HighOutput[13], HighOutput[14], HighOutput[15]);
endmodule

module shift2 (
  input  [31:0] DataInput,
  output [31:0] DataOutput
);

  wire [31:0] shift1_1_dataoutput;

  shift1 shift1_1 (.DataInput(DataInput), .DataOutput(shift1_1_dataoutput));
  shift1 shift1_2 (.DataInput(shift1_1_dataoutput), .DataOutput(DataOutput));
endmodule

module shift4 (
  input  [31:0] DataInput,
  output [31:0] DataOutput
);

  wire [31:0] shift2_1_dataoutput;

  shift2 shift2_1 (.DataInput(DataInput), .DataOutput(shift2_1_dataoutput));
  shift2 shift2_2 (.DataInput(shift2_1_dataoutput), .DataOutput(DataOutput));
endmodule

module shift8 (
  input  [31:0] DataInput,
  output [31:0] DataOutput
);

  wire [31:0] shift4_1_dataoutput;

  shift4 shift4_1 (.DataInput(DataInput), .DataOutput(shift4_1_dataoutput));
  shift4 shift4_2 (.DataInput(shift4_1_dataoutput), .DataOutput(DataOutput));
endmodule

module miniadder (
  input  AInput,
  input  BInput,
  input  CInput,
  output HighOutput,
  output LowOutput
);

  wire and_1_out, and_2_out, xor_1_out;

  xor xor_1 (xor_1_out, AInput, BInput);
  and and_1 (and_1_out, AInput, BInput);
  xor xor_2 (LowOutput, xor_1_out, CInput);
  and and_2 (and_2_out, xor_1_out, CInput);
  or or_1 (HighOutput, and_1_out, and_2_out);
endmodule

module minihalfadder (
  input  AInput,
  input  BInput,
  output [1:0] DataOutput
);

  xor xor_1 (DataOutput[1], AInput, BInput);
  and and_1 (DataOutput[0], AInput, BInput);
endmodule

module big2little (
  input  [31:0] DataInput,
  output [15:0] DataOutput
);


  assign DataOutput = DataInput[31:16];
endmodule

module megaadder (
  input  [31:0] AInput,
  input  [31:0] BInput,
  output [31:0] DataOutput
);

  wire claadder_2_cout;

  CLAAdder claadder_1 (
    .AInput(AInput[15:0]), .BInput(BInput[15:0]), .Cin(claadder_2_cout), .NumberOutput(DataOutput[15:0]));  // open: Cout, Vout
  CLAAdder claadder_2 (
    .AInput(AInput[31:16]), .BInput(BInput[31:16]), .Cout(claadder_2_cout), .NumberOutput(DataOutput[31:16]));  // open: Cin, Vout
endmodule

module shorttoint (
  input  [15:0] DataInput,
  output [31:0] DataOutput
);


  assign DataOutput = {DataInput, {16{1'b0}}};
endmodule

module logicgates (
  input  [15:0] AInput,
  input  [15:0] BInput,
  input  [1:0] Operation,
  output [15:0] DataOutput
);

  wire and_1_out, and_2_out, and_3_out, and_4_out, not_1_out, not_2_out, not_3_out, not_4_out;
  wire [15:0] and_5_out, and_6_out, and_7_out, and_8_out, and_9_out, bit_extender_1_out, bit_extender_2_out,
       bit_extender_3_out, bit_extender_4_out, not_5_out, or_1_out, xor_1_out;

  and and_1 (and_1_out, Operation[0], Operation[1]);
  not not_1 (not_1_out, Operation[0]);
  and and_2 (and_2_out, not_1_out, not_2_out);
  not not_2 (not_2_out, Operation[1]);
  not not_3 (not_3_out, Operation[0]);
  and and_3 (and_3_out, not_3_out, Operation[1]);
  and and_4 (and_4_out, Operation[0], not_4_out);
  not not_4 (not_4_out, Operation[1]);
  assign not_5_out = ~AInput;  // NOT_Gate not_5, 16 bits wide
  assign bit_extender_1_out = {{15{and_1_out}}, and_1_out};  // Bit_Extender bit_extender_1
  assign and_5_out = AInput & BInput;  // AND_Gate and_5, 16 bits wide
  assign bit_extender_2_out = {{15{and_2_out}}, and_2_out};  // Bit_Extender bit_extender_2
  assign or_1_out = AInput | BInput;  // OR_Gate or_1, 16 bits wide
  assign bit_extender_3_out = {{15{and_3_out}}, and_3_out};  // Bit_Extender bit_extender_3
  assign xor_1_out = AInput ^ BInput;  // XOR_Gate xor_1, 16 bits wide
  assign bit_extender_4_out = {{15{and_4_out}}, and_4_out};  // Bit_Extender bit_extender_4
  assign DataOutput = and_6_out | and_7_out | and_8_out | and_9_out;  // OR_Gate or_2, 16 bits wide
  assign and_6_out = not_5_out & bit_extender_1_out;  // AND_Gate and_6, 16 bits wide
  assign and_7_out = and_5_out & bit_extender_2_out;  // AND_Gate and_7, 16 bits wide
  assign and_8_out = or_1_out & bit_extender_3_out;  // AND_Gate and_8, 16 bits wide
  assign and_9_out = xor_1_out & bit_extender_4_out;  // AND_Gate and_9, 16 bits wide
endmodule

module popcountadder0 (
  input  [1:0] AInput,
  input  [1:0] BInput,
  output [2:0] out_3
);

  wire minihalfadder2output_1_highoutput;

  miniadder miniadder_1 (
    .AInput(AInput[0]), .BInput(BInput[0]), .CInput(minihalfadder2output_1_highoutput),
    .HighOutput(out_3[0]), .LowOutput(out_3[1]));
  minihalfadder2output minihalfadder2output_1 (
    .AInput(AInput[1]), .BInput(BInput[1]), .HighOutput(minihalfadder2output_1_highoutput),
    .LowOutput(out_3[2]));
endmodule

module popcountadder1 (
  input  [2:0] AInput,
  input  [2:0] BInput,
  output [3:0] DataOutput
);

  wire miniadder_2_highoutput, minihalfadder2output_1_highoutput;

  miniadder miniadder_1 (
    .AInput(AInput[0]), .BInput(BInput[0]), .CInput(miniadder_2_highoutput), .HighOutput(DataOutput[0]),
    .LowOutput(DataOutput[1]));
  miniadder miniadder_2 (
    .AInput(AInput[1]), .BInput(BInput[1]), .CInput(minihalfadder2output_1_highoutput),
    .HighOutput(miniadder_2_highoutput), .LowOutput(DataOutput[2]));
  minihalfadder2output minihalfadder2output_1 (
    .AInput(AInput[2]), .BInput(BInput[2]), .HighOutput(minihalfadder2output_1_highoutput),
    .LowOutput(DataOutput[3]));
endmodule

module minihalfadder2output (
  input  AInput,
  input  BInput,
  output HighOutput,
  output LowOutput
);

  xor xor_1 (LowOutput, AInput, BInput);
  and and_1 (HighOutput, AInput, BInput);
endmodule

module halfbyteadder (
  input  [3:0] AInput,
  input  [3:0] BInput,
  output [4:0] DataOutput
);

  wire miniadder_2_highoutput, miniadder_3_highoutput, miniadder_4_highoutput;

  miniadder miniadder_1 (
    .AInput(AInput[0]), .BInput(BInput[0]), .CInput(miniadder_2_highoutput), .HighOutput(DataOutput[0]),
    .LowOutput(DataOutput[1]));
  miniadder miniadder_2 (
    .AInput(AInput[1]), .BInput(BInput[1]), .CInput(miniadder_3_highoutput),
    .HighOutput(miniadder_2_highoutput), .LowOutput(DataOutput[2]));
  miniadder miniadder_3 (
    .AInput(AInput[2]), .BInput(BInput[2]), .CInput(miniadder_4_highoutput),
    .HighOutput(miniadder_3_highoutput), .LowOutput(DataOutput[3]));
  miniadder miniadder_4 (
    .AInput(AInput[3]), .BInput(BInput[3]), .HighOutput(miniadder_4_highoutput), .LowOutput(DataOutput[4]));  // open: CInput
endmodule

module rolshift1 (
  input  RolInput,
  input  [15:0] DataInput,
  output RolOutput,
  output [15:0] DataOutput
);

  and and_1 (DataOutput[15], RolInput, DataInput[0]);

  assign DataOutput[14:0] = DataInput[15:1];
  assign RolOutput = RolInput;
endmodule

module rolshift2 (
  input  RolInput,
  input  [15:0] DataInput,
  output RolOutput,
  output [15:0] DataOutput
);

  wire rolshift1_1_roloutput;
  wire [15:0] rolshift1_1_dataoutput;

  rolshift1 rolshift1_1 (
    .RolInput(RolInput), .DataInput(DataInput), .RolOutput(rolshift1_1_roloutput),
    .DataOutput(rolshift1_1_dataoutput));
  rolshift1 rolshift1_2 (
    .RolInput(rolshift1_1_roloutput), .DataInput(rolshift1_1_dataoutput), .RolOutput(RolOutput),
    .DataOutput(DataOutput));
endmodule

module rolshift4 (
  input  RolInput,
  input  [15:0] DataInput,
  output RolOutput,
  output [15:0] DataOutput
);

  wire rolshift2_1_roloutput;
  wire [15:0] rolshift2_1_dataoutput;

  rolshift2 rolshift2_1 (
    .RolInput(RolInput), .DataInput(DataInput), .RolOutput(rolshift2_1_roloutput),
    .DataOutput(rolshift2_1_dataoutput));
  rolshift2 rolshift2_2 (
    .RolInput(rolshift2_1_roloutput), .DataInput(rolshift2_1_dataoutput), .RolOutput(RolOutput),
    .DataOutput(DataOutput));
endmodule

module rolshift8 (
  input  RolInput,
  input  [15:0] DataInput,
  output RolOutput,
  output [15:0] DataOutput
);

  wire rolshift4_1_roloutput;
  wire [15:0] rolshift4_1_dataoutput;

  rolshift4 rolshift4_1 (
    .RolInput(RolInput), .DataInput(DataInput), .RolOutput(rolshift4_1_roloutput),
    .DataOutput(rolshift4_1_dataoutput));
  rolshift4 rolshift4_2 (
    .RolInput(rolshift4_1_roloutput), .DataInput(rolshift4_1_dataoutput), .RolOutput(RolOutput),
    .DataOutput(DataOutput));
endmodule

module mininoCoutAdder (
  input  AInput,
  input  BInput,
  input  CInput,
  output LowOutput
);

  wire xor_1_out;

  xor xor_1 (xor_1_out, AInput, BInput);
  xor xor_2 (LowOutput, xor_1_out, CInput);
endmodule

module XORAdder (
  input  [15:0] AInput,
  input  [15:0] BInput,
  input  [15:0] CInput,
  output [15:0] DataOutput
);

  mininoCoutAdder mininocoutadder_1 (
    .AInput(AInput[0]), .BInput(BInput[0]), .CInput(CInput[0]), .LowOutput(DataOutput[0]));
  mininoCoutAdder mininocoutadder_2 (
    .AInput(AInput[1]), .BInput(BInput[1]), .CInput(CInput[1]), .LowOutput(DataOutput[1]));
  mininoCoutAdder mininocoutadder_3 (
    .AInput(AInput[2]), .BInput(BInput[2]), .CInput(CInput[2]), .LowOutput(DataOutput[2]));
  mininoCoutAdder mininocoutadder_4 (
    .AInput(AInput[3]), .BInput(BInput[3]), .CInput(CInput[3]), .LowOutput(DataOutput[3]));
  mininoCoutAdder mininocoutadder_5 (
    .AInput(AInput[4]), .BInput(BInput[4]), .CInput(CInput[4]), .LowOutput(DataOutput[4]));
  mininoCoutAdder mininocoutadder_6 (
    .AInput(AInput[5]), .BInput(BInput[5]), .CInput(CInput[5]), .LowOutput(DataOutput[5]));
  mininoCoutAdder mininocoutadder_7 (
    .AInput(AInput[6]), .BInput(BInput[6]), .CInput(CInput[6]), .LowOutput(DataOutput[6]));
  mininoCoutAdder mininocoutadder_8 (
    .AInput(AInput[7]), .BInput(BInput[7]), .CInput(CInput[7]), .LowOutput(DataOutput[7]));
  mininoCoutAdder mininocoutadder_9 (
    .AInput(AInput[8]), .BInput(BInput[8]), .CInput(CInput[8]), .LowOutput(DataOutput[8]));
  mininoCoutAdder mininocoutadder_10 (
    .AInput(AInput[9]), .BInput(BInput[9]), .CInput(CInput[9]), .LowOutput(DataOutput[9]));
  mininoCoutAdder mininocoutadder_11 (
    .AInput(AInput[10]), .BInput(BInput[10]), .CInput(CInput[10]), .LowOutput(DataOutput[10]));
  mininoCoutAdder mininocoutadder_12 (
    .AInput(AInput[11]), .BInput(BInput[11]), .CInput(CInput[11]), .LowOutput(DataOutput[11]));
  mininoCoutAdder mininocoutadder_13 (
    .AInput(AInput[12]), .BInput(BInput[12]), .CInput(CInput[12]), .LowOutput(DataOutput[12]));
  mininoCoutAdder mininocoutadder_14 (
    .AInput(AInput[13]), .BInput(BInput[13]), .CInput(CInput[13]), .LowOutput(DataOutput[13]));
  mininoCoutAdder mininocoutadder_15 (
    .AInput(AInput[14]), .BInput(BInput[14]), .CInput(CInput[14]), .LowOutput(DataOutput[14]));
  mininoCoutAdder mininocoutadder_16 (
    .AInput(AInput[15]), .BInput(BInput[15]), .CInput(CInput[15]), .LowOutput(DataOutput[15]));
endmodule

module CLAAdder (
  input  [15:0] AInput,
  input  [15:0] BInput,
  input  Cin,
  output Cout,
  output Vout,
  output [15:0] NumberOutput
);

  wire [2:0] GlobalLAU_cout;
  wire [3:0] C0, C1, C2, C3, G0, G1, G2, G3, GR, P0, P1, P2, P3, PR;
  wire [15:0] AInput_t, BInput_t, xoradder_1_dataoutput;

  reverse reverse_1 (.DataInput(AInput), .DataOutput(AInput_t));
  reverse reverse_2 (.DataInput(BInput), .DataOutput(BInput_t));
  assign {P3, P2, P1, P0} = AInput_t ^ BInput_t;  // XOR_Gate xor_1, 16 bits wide
  assign {G3, G2, G1, G0} = AInput_t & BInput_t;  // AND_Gate and_1, 16 bits wide
  LAU4 GlobalLAU (.PInput(PR), .GInput(GR), .Cin(Cin), .Cout({Cout, GlobalLAU_cout}));  // open: PResume, GResume
  XORAdder xoradder_1 (
    .AInput(AInput_t), .BInput(BInput_t), .CInput({C3[2:0], C2, C1, C0, Cin}),
    .DataOutput(xoradder_1_dataoutput));
  LAU4 lau4_1 (.PInput(P3), .GInput(G3), .Cin(GlobalLAU_cout[2]), .Cout(C3), .PResume(PR[3]), .GResume(GR[3]));
  LAU4 lau4_2 (.PInput(P2), .GInput(G2), .Cin(GlobalLAU_cout[1]), .Cout(C2), .PResume(PR[2]), .GResume(GR[2]));
  LAU4 lau4_3 (.PInput(P1), .GInput(G1), .Cin(GlobalLAU_cout[0]), .Cout(C1), .PResume(PR[1]), .GResume(GR[1]));
  LAU4 lau4_4 (.PInput(P0), .GInput(G0), .Cin(Cin), .Cout(C0), .PResume(PR[0]), .GResume(GR[0]));
  reverse reverse_3 (.DataInput(xoradder_1_dataoutput), .DataOutput(NumberOutput));
  xor xor_2 (Vout, C3[3], C3[2]);

  // Other names for the same wires on the sheet: Cout_t[15:0] = {C3[2:0], C2, C1, C0, Cin}
endmodule

module LAU4 (
  input  [3:0] PInput,
  input  [3:0] GInput,
  input  Cin,
  output [3:0] Cout,
  output PResume,
  output GResume
);

  wire and_1_out, and_2_out, and_3_out, and_4_out, and_5_out, and_6_out, and_7_out, and_8_out, and_9_out,
       and_10_out, and_11_out, and_13_out, and_14_out;

  and and_1 (and_1_out, PInput[2], PInput[1], PInput[0], Cin);
  and and_2 (and_2_out, PInput[3], PInput[2], PInput[1], GInput[0]);
  and and_3 (and_3_out, PInput[2], PInput[1], GInput[0]);
  and and_4 (and_4_out, PInput[3], PInput[2], GInput[1]);
  and and_5 (and_5_out, PInput[2], GInput[1]);
  and and_6 (and_6_out, PInput[1], PInput[0], Cin);
  and and_7 (and_7_out, PInput[3], PInput[2], PInput[1], GInput[0]);
  and and_8 (and_8_out, PInput[3], PInput[2], PInput[1], PInput[0], Cin);
  and and_9 (and_9_out, PInput[3], GInput[2]);
  and and_10 (and_10_out, PInput[1], GInput[0]);
  and and_11 (and_11_out, PInput[0], Cin);
  and and_12 (PResume, PInput[3], PInput[2], PInput[1], PInput[0]);
  and and_13 (and_13_out, GInput[1], PInput[2], PInput[3]);
  or or_1 (Cout[3], and_8_out, and_2_out, and_4_out, and_9_out, GInput[3]);
  or or_2 (Cout[2], and_1_out, and_3_out, and_5_out, GInput[2]);
  or or_3 (Cout[1], and_6_out, and_10_out, GInput[1]);
  or or_4 (Cout[0], and_11_out, GInput[0]);
  and and_14 (and_14_out, GInput[2], PInput[3]);
  or or_5 (GResume, and_7_out, and_13_out, and_14_out, GInput[3]);

  // Other names for the same wires on the sheet: G0 = GInput[0]; G1 = GInput[1]; G2 = GInput[2]; G3 = GInput[3];
  //   P0 = PInput[0]; P1 = PInput[1]; P2 = PInput[2]; P3 = PInput[3]
endmodule

module addsub (
  input  [15:0] AInput,
  input  [15:0] BInput,
  input  Operation,
  input  Cin,
  output Cout,
  output Vout,
  output [15:0] NumberOutput
);

  wire xor_2_out;
  wire [15:0] bit_extender_1_out, xor_1_out;

  assign xor_1_out = BInput ^ bit_extender_1_out;  // XOR_Gate xor_1, 16 bits wide
  assign bit_extender_1_out = {{15{Operation}}, Operation};  // Bit_Extender bit_extender_1
  xor xor_2 (xor_2_out, Operation, Cin);
  CLAAdder claadder_1 (
    .AInput(AInput), .BInput(xor_1_out), .Cin(xor_2_out), .Cout(Cout), .Vout(Vout),
    .NumberOutput(NumberOutput));
endmodule
